// Logisim project mipsVersion2.circ as structural Verilog: 20 circuits, main circuit MIPS32
module MIPS32 (
);

  wire aluimmediateopcircuit_1_beq, aluimmediateopcircuit_1_bgez, aluimmediateopcircuit_1_bgtz,
       aluimmediateopcircuit_1_blez, aluimmediateopcircuit_1_bltz, aluimmediateopcircuit_1_bne,
       aluimmediateopcircuit_1_j, aluimmediateopcircuit_1_jal, aluimmediateopcircuit_1_lui,
       aluopcoderrtypeinstruction_1_jalr, aluopcoderrtypeinstruction_1_jr, ALUSrc_q, and_1_out, and_2_out,
       and_4_out, and_5_out, and_6_out, and_7_out, and_8_out, Clk, control_decoder_1_aluop0,
       control_decoder_1_aluop1, control_decoder_1_alusrc, control_decoder_1_regdst, detect_hazard_1_hazard,
       EX_Mem_WE, Haz_Fwd_q, ID_EX_WE, idetect_hazard_1_ex_m__ra, idetect_hazard_1_ex_m__rb,
       idetect_hazard_1_hazard, idetect_hazard_1_m_wb__ra, idetect_hazard_1_m_wb__rb, load_hazard, M_WB_WE,
       MovE, Move_Enable_2_q, Move_Enable_3_q, Move_Enable_q, multiplexer_5_out, multiplexer_16_out,
       multiplexer_26_out, multiplexer_27_out, multiplexer_28_out, multiplexer_31_out, not_1_out, or_1_out,
       RegWr, RegWr_2_q, RegWr_3_q, RegWr_q, WB_Ctrl, WB_Ctrl_2_q, WB_Ctrl_3_q, WB_Ctrl_q;
  wire [0:0] aluopcoderrtypeinstruction_1_shift_src;
  wire [1:0] aluimmediateopcircuit_1_sltyes, aluopcoderrtypeinstruction_1_movz,
       aluopcoderrtypeinstruction_1_sltyes, forwarding_1_a, forwarding_1_b, idforwarding_1_a,
       idforwarding_1_b, jumping_1_link, link_jump_2_q, link_jump_3_q, link_jump_q, mov_controls_q,
       multiplexer_7_out, multiplexer_18_out, multiplexer_24_out, multiplexer_34_out, register_1_q,
       slt_controls_q;
  wire [3:0] aluimmediateopcircuit_1_op0, ALUOpCode_q, aluopcoderrtypeinstruction_1_op0,
       control_decoder_1_memdata, MemData_q, multiplexer_6_out, multiplexer_17_out, multiplexer_20_out,
       multiplexer_35_out;
  wire [4:0] bit_extender_1_out, ERD, EX_MEM_Ra, ID_EX_Ra, ID_EX_Rb, MRD, multiplexer_8_out,
       multiplexer_9_out, multiplexer_10_out, multiplexer_15_out, multiplexer_19_out, multiplexer_29_out,
       multiplexer_30_out, rA, rB, registerfile_1_p4, rW, RW_2_q, RW_q, WRD;
  wire [5:0] Inst_q_2, mipsprogramrom_1_p2, multiplexer_36_out, SHAMT_src_q;
  wire [6:0] ex_1_memdata_2, MemData_2_q, MemData_3_q;
  wire [15:6] Inst_q;
  wire [29:0] incrementer_1_p1, incrementer_1_p2;
  wire [31:0] A, A_q, ALU_Out_2_q, ALU_Out_q, B, B_q, bit_extender_2_out, bit_extender_3_out,
       branching_1_pcrel, byteshift_1_c, byteshiftright_1_c, ex_1_b_2, ex_1_d, Imm_q, jumping_1_pc_8,
       jumping_1_pcabs, loading_1_b, Memory_Out_2_q, Memory_Out_q, mips_ram_1_p8, mipsprogramrom_1_p1,
       multiplexer_1_out, multiplexer_2_out, multiplexer_3_out, multiplexer_4_out, multiplexer_12_out,
       multiplexer_13_out, multiplexer_14_out, multiplexer_21_out, multiplexer_22_out, multiplexer_23_out,
       multiplexer_25_out, multiplexer_33_out, multiplexer_38_out, multiplexer_39_out, multiplexer_40_out,
       PC_4_2_q, PC_4_q, pcabs_2_q, pcabs_q, pcrel_2_q, pcrel_q, registerfile_1_p1, registerfile_1_p7,
       registerfile_1_p8, return_addr_2_q, return_addr_3_q, return_addr_q;

  Clock clock_1 (.out(Clk));
  // Incrementer incrementer_1: pin names not known; wires that end beside it: incrementer_1_p1, incrementer_1_p2
  Multiplexer #(.width(32), .enable("false")) multiplexer_1 (
    .in0({incrementer_1_p2, register_1_q}), .in1(jumping_1_pcabs), .out(multiplexer_1_out),
    .sel(jumping_1_link[1]));
  Multiplexer #(.width(32), .enable("false")) multiplexer_2 (
    .in0(multiplexer_1_out), .in1(branching_1_pcrel), .out(multiplexer_2_out), .sel(or_1_out));
  Multiplexer #(.width(32), .enable("false")) multiplexer_3 (
    .in0(multiplexer_2_out), .in1({incrementer_1_p1, register_1_q}), .out(multiplexer_3_out),
    .sel(load_hazard));
  // MIPSProgramROM mipsprogramrom_1: pin names not known; wires that end beside it: mipsprogramrom_1_p1, mipsprogramrom_1_p2[1:0]
  Register #(.width(32)) register_1 (
    .D(multiplexer_3_out), .Q({incrementer_1_p1, register_1_q}), .clk(Clk));  // open: en, clr
  Multiplexer #(.width(32), .enable("false")) multiplexer_4 (
    .in0(mipsprogramrom_1_p1),
    .in1({Inst_q_2[5], bit_extender_1_out[4], Inst_q_2[3:0], rA, rB, Inst_q, mipsprogramrom_1_p2}),
    .out(multiplexer_4_out), .sel(load_hazard));
  Register #(.width(32)) Inst (
    .D(multiplexer_4_out),
    .Q({Inst_q_2[5], bit_extender_1_out[4], Inst_q_2[3:0], rA, rB, Inst_q, mipsprogramrom_1_p2}), .clk(Clk));  // open: en, clr
  and and_1 (and_1_out, ~mipsprogramrom_1_p2[5], ~mipsprogramrom_1_p2[4], mipsprogramrom_1_p2[3], mipsprogramrom_1_p2[1]);  // AND_Gate
  and and_2 (and_2_out, ~Inst_q_2[5], ~bit_extender_1_out[4], ~Inst_q_2[3], ~Inst_q_2[1], ~Inst_q_2[0], ~Inst_q_2[2]);  // AND_Gate
  and and_3 (MovE, and_1_out, ~control_decoder_1_alusrc);  // AND_Gate
  Control_Decoder control_decoder_1 (
    .func(mipsprogramrom_1_p2), .Op({Inst_q_2[5], bit_extender_1_out[4], Inst_q_2[3:0]}), .rt(rB),
    .RegDst(control_decoder_1_regdst), .RegWr(RegWr), .ALUSrc(control_decoder_1_alusrc),
    .ALUOp1(control_decoder_1_aluop1), .ALUOp0(control_decoder_1_aluop0),
    .MemData(control_decoder_1_memdata), .MemToReg(WB_Ctrl));
  Multiplexer #(.enable("false")) multiplexer_5 (
    .in0(RegWr_3_q), .in1(M_WB_WE), .out(multiplexer_5_out), .sel(Move_Enable_3_q));
  ALUImmediateOPCircuit aluimmediateopcircuit_1 (
    .bit5(Inst_q_2[5]), .bit4(bit_extender_1_out[4]), .bit3(Inst_q_2[3]), .bit2(Inst_q_2[2]),
    .bit1(Inst_q_2[1]), .bit0(Inst_q_2[0]), .rt(rB), .aluOp1(control_decoder_1_aluop1),
    .aluOp0(control_decoder_1_aluop0), .op3(aluimmediateopcircuit_1_op0[3]),
    .op2(aluimmediateopcircuit_1_op0[2]), .op1(aluimmediateopcircuit_1_op0[1]),
    .op0(aluimmediateopcircuit_1_op0[0]), .bltz(aluimmediateopcircuit_1_bltz),
    .bgez(aluimmediateopcircuit_1_bgez), .sltunsigned(aluimmediateopcircuit_1_sltyes[1]),
    .sltyes(aluimmediateopcircuit_1_sltyes[0]), .j(aluimmediateopcircuit_1_j),
    .jal(aluimmediateopcircuit_1_jal), .beq(aluimmediateopcircuit_1_beq), .bne(aluimmediateopcircuit_1_bne),
    .blez(aluimmediateopcircuit_1_blez), .bgtz(aluimmediateopcircuit_1_bgtz),
    .LUI(aluimmediateopcircuit_1_lui));
  not not_1 (not_1_out, aluimmediateopcircuit_1_lui);
  assign bit_extender_1_out[3:0] = {{3{not_1_out}}, not_1_out};  // Bit_Extender bit_extender_1
  Branching branching_1 (
    .B(B), .A(A), .PC_4({incrementer_1_p1, register_1_q}), .Imm({Inst_q, mipsprogramrom_1_p2}),
    .bgtz(aluimmediateopcircuit_1_bgtz), .blez(aluimmediateopcircuit_1_blez),
    .bgez(aluimmediateopcircuit_1_bgez), .bltz(aluimmediateopcircuit_1_bltz),
    .beq(aluimmediateopcircuit_1_beq), .bne(aluimmediateopcircuit_1_bne), .pcrel(branching_1_pcrel));
  Multiplexer #(.width(4), .enable("false")) multiplexer_6 (
    .in0(aluimmediateopcircuit_1_op0), .in1(bit_extender_1_out[3:0]), .out(multiplexer_6_out),
    .sel(aluimmediateopcircuit_1_lui));
  Jumping jumping_1 (
    .Inst({rA, rB, Inst_q, mipsprogramrom_1_p2}), .PC_4({incrementer_1_p1, register_1_q}),
    .jal(aluimmediateopcircuit_1_jal), .j(aluimmediateopcircuit_1_j), .A(A), .jr(and_7_out),
    .jalr(and_6_out), .jump(jumping_1_link[1]), .link(jumping_1_link[0]), .pcabs(jumping_1_pcabs),
    .PC_8(jumping_1_pc_8));
  and and_4 (and_4_out, ~MemData_3_q[5], multiplexer_5_out);  // AND_Gate
  Multiplexer #(.width(2), .enable("false")) multiplexer_7 (
    .in0(aluimmediateopcircuit_1_sltyes), .in1(aluopcoderrtypeinstruction_1_sltyes), .out(multiplexer_7_out),
    .sel(and_2_out));
  or or_1 (or_1_out, aluimmediateopcircuit_1_bgtz, aluimmediateopcircuit_1_blez, aluimmediateopcircuit_1_bne, aluimmediateopcircuit_1_beq, aluimmediateopcircuit_1_bgez, aluimmediateopcircuit_1_bltz);
  Multiplexer #(.width(5), .enable("false")) multiplexer_8 (
    .in0(Inst_q[15:11]), .in1(rB), .out(multiplexer_8_out), .sel(control_decoder_1_regdst));
  ALUOpCoderRTypeInstruction aluopcoderrtypeinstruction_1 (
    .ALUOp1(control_decoder_1_aluop1), .ALUOp2(control_decoder_1_aluop0), .func5(mipsprogramrom_1_p2[5]),
    .func4(mipsprogramrom_1_p2[4]), .func3(mipsprogramrom_1_p2[3]), .func2(mipsprogramrom_1_p2[2]),
    .func1(mipsprogramrom_1_p2[1]), .func0(mipsprogramrom_1_p2[0]),
    .op3(aluopcoderrtypeinstruction_1_op0[3]), .op2(aluopcoderrtypeinstruction_1_op0[2]),
    .op1(aluopcoderrtypeinstruction_1_op0[1]), .op0(aluopcoderrtypeinstruction_1_op0[0]),
    .movn(aluopcoderrtypeinstruction_1_movz[1]), .movz(aluopcoderrtypeinstruction_1_movz[0]),
    .shift_src(aluopcoderrtypeinstruction_1_shift_src[0]), .JALR(aluopcoderrtypeinstruction_1_jalr),
    .JR(aluopcoderrtypeinstruction_1_jr), .sltyes(aluopcoderrtypeinstruction_1_sltyes[0]),
    .sltunsignedcheck(aluopcoderrtypeinstruction_1_sltyes[1]));
  and and_5 (and_5_out, ~mipsprogramrom_1_p2[5], ~mipsprogramrom_1_p2[4], mipsprogramrom_1_p2[2], ~mipsprogramrom_1_p2[3]);  // AND_Gate
  and and_6 (and_6_out, and_2_out, aluopcoderrtypeinstruction_1_jalr);
  and and_7 (and_7_out, aluopcoderrtypeinstruction_1_jr, and_2_out);
  Multiplexer #(.width(5), .enable("false")) multiplexer_9 (
    .in0(Inst_q[10:6]), .in1(rA), .out(multiplexer_9_out), .sel(and_5_out));
  Detect_Hazard detect_hazard_1 (
    .ID_EX_RD(ERD), .EX_MEM_rd(WRD), .MEM_WB_rd(MRD), .rA(rA), .rB(rB), .Hazard(detect_hazard_1_hazard));
  // RegisterFile registerfile_1: pin names not known; wires that end beside it: registerfile_1_p1, Clk, and_4_out, registerfile_1_p4, rA, rB, registerfile_1_p7, registerfile_1_p8
  assign bit_extender_2_out = {{16{Inst_q[15]}}, {Inst_q, mipsprogramrom_1_p2}};  // Bit_Extender bit_extender_2
  assign bit_extender_3_out = {{16{1'b0}}, {Inst_q, mipsprogramrom_1_p2}};  // Bit_Extender bit_extender_3
  Multiplexer #(.width(5), .enable("false")) multiplexer_10 (
    .in0(multiplexer_9_out), .in1(bit_extender_1_out), .out(multiplexer_10_out), .sel(bit_extender_1_out[4]));
  Detect_Load_Use detect_load_use_1 (
    .ID_EX_rT(ERD), .ID_EX_MemRead(MemData_q[0]), .rA(rA), .rB(rB), .Hazard(load_hazard));
  IDetect_Hazard idetect_hazard_1 (
    .EX_MEM_rd(ERD), .MEM_WB_rd(MRD), .rA(rA), .rB(rB), .Hazard(idetect_hazard_1_hazard),
    .EX_M__rB(idetect_hazard_1_ex_m__rb), .M_WB__rB(idetect_hazard_1_m_wb__rb),
    .EX_M__rA(idetect_hazard_1_ex_m__ra), .M_WB__rA(idetect_hazard_1_m_wb__ra));
  Multiplexer #(.width(5), .enable("false")) multiplexer_11 (
    .in0(multiplexer_8_out), .in1({5{1'b1}}), .out(rW), .sel(aluimmediateopcircuit_1_jal));
  Multiplexer #(.width(32), .enable("false")) multiplexer_12 (
    .in0(bit_extender_2_out), .in1(bit_extender_3_out), .out(multiplexer_12_out), .sel(and_8_out));
  Multiplexer #(.width(32), .enable("false")) multiplexer_13 (
    .in0(registerfile_1_p7), .in1({32{1'b0}}), .out(multiplexer_13_out), .sel(load_hazard));
  Multiplexer #(.width(32), .enable("false")) multiplexer_14 (
    .in0(registerfile_1_p8), .in1({32{1'b0}}), .out(multiplexer_14_out), .sel(load_hazard));
  Multiplexer #(.width(5), .enable("false")) multiplexer_15 (
    .in0(rW), .in1({5{1'b0}}), .out(multiplexer_15_out), .sel(load_hazard));
  Multiplexer #(.enable("false")) multiplexer_16 (
    .in0(control_decoder_1_alusrc), .in1(1'b0), .out(multiplexer_16_out), .sel(load_hazard));
  and and_8 (and_8_out, multiplexer_17_out[3], ~multiplexer_17_out[0]);  // AND_Gate
  Multiplexer #(.width(4), .enable("false")) multiplexer_17 (
    .in0(multiplexer_6_out), .in1(aluopcoderrtypeinstruction_1_op0), .out(multiplexer_17_out), .sel(and_2_out));
  Multiplexer #(.width(2), .enable("false")) multiplexer_18 (
    .in0(multiplexer_7_out), .in1(2'b00), .out(multiplexer_18_out), .sel(load_hazard));
  Multiplexer #(.width(5), .enable("false")) multiplexer_19 (
    .in0(rW), .in1({5{1'b0}}), .out(multiplexer_19_out), .sel(load_hazard));
  Multiplexer #(.width(4), .enable("false")) multiplexer_20 (
    .in0(control_decoder_1_memdata), .in1(4'b0000), .out(multiplexer_20_out), .sel(load_hazard));
  Multiplexer #(.width(32), .enable("false")) multiplexer_21 (
    .in0(branching_1_pcrel), .in1({32{1'b0}}), .out(multiplexer_21_out), .sel(load_hazard));
  Multiplexer #(.width(32), .enable("false")) multiplexer_22 (
    .in0(jumping_1_pcabs), .in1({32{1'b0}}), .out(multiplexer_22_out), .sel(load_hazard));
  Multiplexer #(.width(32), .enable("false")) multiplexer_23 (
    .in0(jumping_1_pc_8), .in1({32{1'b0}}), .out(multiplexer_23_out), .sel(load_hazard));
  Multiplexer #(.width(2), .enable("false")) multiplexer_24 (
    .in0(jumping_1_link), .in1(2'b00), .out(multiplexer_24_out), .sel(load_hazard));
  Multiplexer #(.width(32), .enable("false")) multiplexer_25 (
    .in0({incrementer_1_p1, register_1_q}), .in1({32{1'b0}}), .out(multiplexer_25_out), .sel(load_hazard));
  Multiplexer #(.enable("false")) multiplexer_26 (.in0(MovE), .in1(1'b0), .out(multiplexer_26_out), .sel(load_hazard));
  Multiplexer #(.enable("false")) multiplexer_27 (
    .in0(WB_Ctrl), .in1(1'b0), .out(multiplexer_27_out), .sel(load_hazard));
  Multiplexer #(.enable("false")) multiplexer_28 (
    .in0(detect_hazard_1_hazard), .in1(1'b0), .out(multiplexer_28_out), .sel(load_hazard));
  Multiplexer #(.width(5), .enable("false")) multiplexer_29 (
    .in0(rA), .in1({5{1'b0}}), .out(multiplexer_29_out), .sel(load_hazard));
  Multiplexer #(.width(5), .enable("false")) multiplexer_30 (
    .in0(rB), .in1({5{1'b0}}), .out(multiplexer_30_out), .sel(load_hazard));
  Multiplexer #(.enable("false")) multiplexer_31 (.in0(RegWr), .in1(1'b0), .out(multiplexer_31_out), .sel(load_hazard));
  Multiplexer #(.select(2), .width(32), .enable("false")) multiplexer_32 (
    .in0(ex_1_d), .in1(ALU_Out_q), .in2(multiplexer_14_out), .in3(multiplexer_14_out), .out(B),
    .sel(idforwarding_1_b));
  Multiplexer #(.width(32), .enable("false")) multiplexer_33 (
    .in0(multiplexer_12_out), .in1({32{1'b0}}), .out(multiplexer_33_out), .sel(load_hazard));
  Multiplexer #(.width(2), .enable("false")) multiplexer_34 (
    .in0(aluopcoderrtypeinstruction_1_movz), .in1(2'b00), .out(multiplexer_34_out), .sel(load_hazard));
  Multiplexer #(.width(4), .enable("false")) multiplexer_35 (
    .in0(multiplexer_17_out), .in1(4'b0000), .out(multiplexer_35_out), .sel(load_hazard));
  Multiplexer #(.width(6), .enable("false")) multiplexer_36 (
    .in0({multiplexer_10_out, aluopcoderrtypeinstruction_1_shift_src[0]}), .in1({6{1'b0}}),
    .out(multiplexer_36_out), .sel(load_hazard));
  IDForwarding idforwarding_1 (
    .Hazard(idetect_hazard_1_hazard), .EX_M__rB(idetect_hazard_1_ex_m__rb),
    .M_WB__rB(idetect_hazard_1_m_wb__rb), .EX_M__rA(idetect_hazard_1_ex_m__ra),
    .M_WB__rA(idetect_hazard_1_m_wb__ra), .B(idforwarding_1_b), .A(idforwarding_1_a));
  Register #(.width(32)) u_A (.D(multiplexer_13_out), .Q(A_q), .clk(Clk));  // open: en, clr
  Multiplexer #(.select(2), .width(32), .enable("false")) multiplexer_37 (
    .in0(ex_1_d), .in1(ALU_Out_q), .in2(multiplexer_13_out), .in3(multiplexer_13_out), .out(A),
    .sel(idforwarding_1_a));
  Register #(.width(32)) u_B (.D(multiplexer_14_out), .Q(B_q), .clk(Clk));  // open: en, clr
  Register #(.width(5)) RD_Ctrl (.D(multiplexer_15_out), .Q(ERD), .clk(Clk));  // open: en, clr
  Register #(.width(32)) Imm (.D(multiplexer_33_out), .Q(Imm_q), .clk(Clk));  // open: en, clr
  Register #(.width(1)) ALUSrc (.D(multiplexer_16_out), .Q(ALUSrc_q), .clk(Clk));  // open: en, clr
  Register #(.width(2)) mov_controls (.D(multiplexer_34_out), .Q(mov_controls_q), .clk(Clk));  // open: en, clr
  Register #(.width(4)) ALUOpCode (.D(multiplexer_35_out), .Q(ALUOpCode_q), .clk(Clk));  // open: en, clr
  Register #(.width(6)) SHAMT_src (.D(multiplexer_36_out), .Q(SHAMT_src_q), .clk(Clk));  // open: en, clr
  Register #(.width(2)) slt_controls (.D(multiplexer_18_out), .Q(slt_controls_q), .clk(Clk));  // open: en, clr
  Register #(.width(5)) u_RW (.D(multiplexer_19_out), .Q(RW_q), .clk(Clk));  // open: en, clr
  Register #(.width(4)) MemData (.D(multiplexer_20_out), .Q(MemData_q), .clk(Clk));  // open: en, clr
  Register #(.width(32)) pcrel (.D(multiplexer_21_out), .Q(pcrel_q), .clk(Clk));  // open: en, clr
  Register #(.width(32)) pcabs (.D(multiplexer_22_out), .Q(pcabs_q), .clk(Clk));  // open: en, clr
  Register #(.width(32)) return_addr (.D(multiplexer_23_out), .Q(return_addr_q), .clk(Clk));  // open: en, clr
  Register #(.width(2)) link_jump (.D(multiplexer_24_out), .Q(link_jump_q), .clk(Clk));  // open: en, clr
  Register #(.width(32)) PC_4 (.D(multiplexer_25_out), .Q(PC_4_q), .clk(Clk));  // open: en, clr
  Register #(.width(1)) Move_Enable (.D(multiplexer_26_out), .Q(Move_Enable_q), .clk(Clk));  // open: en, clr
  Register #(.width(1)) u_WB_Ctrl (.D(multiplexer_27_out), .Q(WB_Ctrl_q), .clk(Clk));  // open: en, clr
  Register #(.width(1)) Haz_Fwd (.D(multiplexer_28_out), .Q(Haz_Fwd_q), .clk(Clk));  // open: en, clr
  Register #(.width(5)) u_Ra (.D(multiplexer_29_out), .Q(ID_EX_Ra), .clk(Clk));  // open: en, clr
  Register #(.width(5)) u_Rb (.D(multiplexer_30_out), .Q(ID_EX_Rb), .clk(Clk));  // open: en, clr
  Register #(.width(1)) u_RegWr (.D(multiplexer_31_out), .Q(RegWr_q), .clk(Clk));  // open: en, clr
  Multiplexer #(.select(2), .width(32), .enable("false")) multiplexer_38 (
    .in0(A_q), .in1(registerfile_1_p1), .in2(ALU_Out_q), .in3(ALU_Out_q), .out(multiplexer_38_out),
    .sel(forwarding_1_a));
  Multiplexer #(.select(2), .width(32), .enable("false")) multiplexer_39 (
    .in0(B_q), .in1(registerfile_1_p1), .in2(ALU_Out_q), .in3(ALU_Out_q), .out(multiplexer_39_out),
    .sel(forwarding_1_b));
  Forwarding forwarding_1 (
    .ID_Ex_Rb(ID_EX_Rb), .Hazard(Haz_Fwd_q), .Ex_M_We(EX_Mem_WE), .Ex_M_Rd(MRD), .ID_Ex_Ra(ID_EX_Ra),
    .M_WB_We(M_WB_WE), .M_WB_Rd(WRD), .B(forwarding_1_b), .A(forwarding_1_a));
  EX ex_1 (
    .A(multiplexer_38_out), .B(multiplexer_39_out), .Imm(Imm_q), .ALUSrc(ALUSrc_q), .MemData(MemData_q),
    .MOV(mov_controls_q), .ALUOpCode(ALUOpCode_q), .Shamt(SHAMT_src_q), .SLT(slt_controls_q), .D(ex_1_d),
    .B_2(ex_1_b_2), .MemData_2(ex_1_memdata_2), .WriteEnable(ID_EX_WE));
  Register #(.width(5)) RD_Ctrl_2 (.D(ERD), .Q(MRD), .clk(Clk));  // open: en, clr
  Register #(.width(32)) ALU_Out (.D(ex_1_d), .Q(ALU_Out_q), .clk(Clk));  // open: en, clr
  Register #(.width(32)) Memory_Out (.D(ex_1_b_2), .Q(Memory_Out_q), .clk(Clk));  // open: en, clr
  Register #(.width(7)) MemData_2 (.D(ex_1_memdata_2), .Q(MemData_2_q), .clk(Clk));  // open: en, clr
  Register #(.width(1)) Write_Enable (.D(ID_EX_WE), .Q(EX_Mem_WE), .clk(Clk));  // open: en, clr
  Register #(.width(5)) RW_2 (.D(RW_q), .Q(RW_2_q), .clk(Clk));  // open: en, clr
  Register #(.width(32)) pcrel_2 (.D(pcrel_q), .Q(pcrel_2_q), .clk(Clk));  // open: en, clr
  Register #(.width(32)) pcabs_2 (.D(pcabs_q), .Q(pcabs_2_q), .clk(Clk));  // open: en, clr
  Register #(.width(32)) return_addr_2 (.D(return_addr_q), .Q(return_addr_2_q), .clk(Clk));  // open: en, clr
  Register #(.width(2)) link_jump_2 (.D(link_jump_q), .Q(link_jump_2_q), .clk(Clk));  // open: en, clr
  Register #(.width(32)) PC_4_2 (.D(PC_4_q), .Q(PC_4_2_q), .clk(Clk));  // open: en, clr
  Register #(.width(1)) Move_Enable_2 (.D(Move_Enable_q), .Q(Move_Enable_2_q), .clk(Clk));  // open: en, clr
  Register #(.width(1)) WB_Ctrl_2 (.D(WB_Ctrl_q), .Q(WB_Ctrl_2_q), .clk(Clk));  // open: en, clr
  Register #(.width(5)) Ra_2 (.D(ID_EX_Ra), .Q(EX_MEM_Ra), .clk(Clk));  // open: en, clr
  Register #(.width(1)) RegWr_2 (.D(RegWr_q), .Q(RegWr_2_q), .clk(Clk));  // open: en, clr
  ByteShift byteshift_1 (.B(Memory_Out_q), .Sa(MemData_2_q[4:1]), .C(byteshift_1_c));  // open: sign
  // MIPS_RAM mips_ram_1: pin names not known; wires that end beside it: EX_MEM_Ra, ALU_Out_q[21:2], byteshift_1_c, MemData_2_q[5], MemData_2_q[4:1], Clk, MemData_2_q[0], mips_ram_1_p8
  ByteShiftRight byteshiftright_1 (.B(mips_ram_1_p8), .Sa(MemData_2_q[4:1]), .C(byteshiftright_1_c));  // open: sign
  Loading loading_1 (.A(byteshiftright_1_c), .byte_word(MemData_2_q[4:1]), .lbu(MemData_2_q[6]), .B(loading_1_b));
  Register #(.width(5)) RD_Ctrl_3 (.D(MRD), .Q(WRD), .clk(Clk));  // open: en, clr
  Register #(.width(32)) ALU_Out_2 (.D(ALU_Out_q), .Q(ALU_Out_2_q), .clk(Clk));  // open: en, clr
  Register #(.width(32)) Memory_Out_2 (.D(loading_1_b), .Q(Memory_Out_2_q), .clk(Clk));  // open: en, clr
  Register #(.width(7)) MemData_3 (.D(MemData_2_q), .Q(MemData_3_q), .clk(Clk));  // open: en, clr
  Register #(.width(1)) Write_Enable_2 (.D(EX_Mem_WE), .Q(M_WB_WE), .clk(Clk));  // open: en, clr
  Register #(.width(5)) RW_3 (.D(RW_2_q), .Q(registerfile_1_p4), .clk(Clk));  // open: en, clr
  Register #(.width(32)) pcrel_3 (.D(pcrel_2_q), .clk(Clk));  // open: en, Q, clr
  Register #(.width(32)) pcabs_3 (.D(pcabs_2_q), .clk(Clk));  // open: en, Q, clr
  Register #(.width(32)) return_addr_3 (.D(return_addr_2_q), .Q(return_addr_3_q), .clk(Clk));  // open: en, clr
  Register #(.width(2)) link_jump_3 (.D(link_jump_2_q), .Q(link_jump_3_q), .clk(Clk));  // open: en, clr
  Register #(.width(32)) PC_4_3 (.D(PC_4_2_q), .clk(Clk));  // open: en, Q, clr
  Register #(.width(1)) Move_Enable_3 (.D(Move_Enable_2_q), .Q(Move_Enable_3_q), .clk(Clk));  // open: en, clr
  Register #(.width(1)) WB_Ctrl_3 (.D(WB_Ctrl_2_q), .Q(WB_Ctrl_3_q), .clk(Clk));  // open: en, clr
  Register #(.width(1)) RegWr_3 (.D(RegWr_2_q), .Q(RegWr_3_q), .clk(Clk));  // open: en, clr
  Multiplexer #(.width(32), .enable("false")) multiplexer_40 (
    .in0(ALU_Out_2_q), .in1(Memory_Out_2_q), .out(multiplexer_40_out), .sel(WB_Ctrl_3_q));
  Multiplexer #(.width(32), .enable("false")) multiplexer_41 (
    .in0(multiplexer_40_out), .in1(return_addr_3_q), .out(registerfile_1_p1), .sel(link_jump_3_q[0]));

  // Other names for the same wires on the sheet: ID_EX_Rd[4:0] = ERD

  // Notes on the sheet:
  //   +4
  //   IF/ID
  //   ID
  //   ID/EX
  //   Forwarding
  //   EX/MEM
  //   To Decode Stage
  //   MEM
  //   MEM/WB
  //   PC_Next
  //   WB
endmodule

module EX (
  input  [31:0] A,
  input  [31:0] B,
  input  [31:0] Imm,
  input  ALUSrc,
  input  [3:0] MemData,
  input  [1:0] MOV,
  input  [3:0] ALUOpCode,
  input  [5:0] Shamt,
  input  [1:0] SLT,
  output [31:0] D,
  output [31:0] B_2,
  output [6:0] MemData_2,
  output WriteEnable
);

  wire and_1_out, and_2_out, comparator_1_lt, comparator_2_lt, iszero32_1_out, iszero32_2_out,
       multiplexer_3_out, or_2_out, xor_1_out;
  wire [3:0] bit_extender_4_out, mips_alu_1_p7;
  wire [4:0] bit_extender_3_out, mips_alu_1_p5;
  wire [31:0] adder_1_out, bit_extender_1_out, bit_extender_2_out, mips_alu_1_p6, multiplexer_1_out,
       multiplexer_2_out, multiplexer_5_out, shifter_1_out;

  Multiplexer #(.width(32), .enable("false")) multiplexer_1 (.in0(B), .in1(Imm), .out(multiplexer_1_out), .sel(ALUSrc));
  IsZero32 iszero32_1 (.In(multiplexer_1_out), .Out(iszero32_1_out));
  IsZero32 iszero32_2 (.In(multiplexer_1_out), .Out(iszero32_2_out));
  xor xor_1 (xor_1_out, MOV[0], MOV[1]);
  and and_1 (and_1_out, ~iszero32_1_out, MOV[0]);  // AND_Gate
  and and_2 (and_2_out, iszero32_2_out, MOV[1]);
  assign bit_extender_1_out = {{31{1'b0}}, ALUSrc};  // Bit_Extender bit_extender_1
  or or_1 (WriteEnable, and_1_out, and_2_out);
  Comparator #(.width(32)) comparator_1 (.a(A), .b(multiplexer_1_out), .lt(comparator_1_lt));  // open: gt, eq
  Comparator #(.width(32), .mode("unsigned")) comparator_2 (
    .a(A), .b(multiplexer_1_out), .lt(comparator_2_lt));  // open: gt, eq
  Multiplexer #(.width(32), .enable("false")) multiplexer_2 (
    .in0(multiplexer_1_out), .in1(bit_extender_1_out), .out(multiplexer_2_out), .sel(xor_1_out));
  Multiplexer #(.enable("false")) multiplexer_3 (
    .in0(comparator_1_lt), .in1(comparator_2_lt), .out(multiplexer_3_out), .sel(SLT[1]));
  assign bit_extender_2_out = {{31{1'b0}}, multiplexer_3_out};  // Bit_Extender bit_extender_2
  // Mips_ALU mips_alu_1: pin names not known; wires that end beside it: A, multiplexer_2_out, ALUOpCode, SLT[1], mips_alu_1_p5, mips_alu_1_p6, mips_alu_1_p7[0]
  Multiplexer #(.width(5), .enable("false")) multiplexer_4 (
    .in0(Shamt[5:1]), .in1(bit_extender_3_out), .out(mips_alu_1_p5), .sel(Shamt[0]));
  Bit_Extender #(.in_width(32), .out_width(5), .\type ("sign")) bit_extender_3 (.in(A), .out(bit_extender_3_out));
  Multiplexer #(.width(32), .enable("false")) multiplexer_5 (
    .in0(mips_alu_1_p6), .in1(bit_extender_2_out), .out(multiplexer_5_out), .sel(SLT[0]));
  Shifter #(.width(32)) shifter_1 (.in(A), .\dist (5'b00010), .out(shifter_1_out));
  Adder #(.width(32)) adder_1 (.a(shifter_1_out), .b(Imm), .out(adder_1_out));  // open: cin, cout
  Decoder #(.select(2), .enable("false")) decoder_1 (
    .out0(mips_alu_1_p7[0]), .out1(mips_alu_1_p7[1]), .out2(mips_alu_1_p7[2]), .out3(mips_alu_1_p7[3]),
    .sel(Imm[1:0]));
  assign bit_extender_4_out = {{3{MemData[2]}}, MemData[2]};  // Bit_Extender bit_extender_4
  Multiplexer #(.width(32), .enable("false")) multiplexer_6 (
    .in0(multiplexer_5_out), .in1(adder_1_out), .out(D), .sel(or_2_out));
  or or_2 (or_2_out, MemData[3], MemData[0]);
  assign MemData_2[4:1] = mips_alu_1_p7 | bit_extender_4_out;  // OR_Gate or_3, 4 bits wide

  assign B_2 = B;
  assign {MemData_2[6:5], MemData_2[0]} = {MemData[1], MemData[3], MemData[0]};

  // Notes on the sheet:
  //   MOV
  //   SLT
endmodule

// Det
module Detect_Hazard (
  input  [4:0] rA,
  input  [4:0] rB,
  input  [4:0] ID_EX_RD,
  input  [4:0] EX_MEM_rd,
  input  [4:0] MEM_WB_rd,
  output Hazard
);

  wire and_1_out, and_2_out, isequal5_1_ra, isequal5_2_ra, isequal5_3_ra, isequal5_4_ra, isequal5_5_ra,
       isequal5_6_ra, or_1_out, or_2_out, or_3_out, or_4_out;

  or or_1 (or_1_out, rA[4], rA[3], rA[2], rA[1], rA[0]);
  IsEqual5 isequal5_1 (.in_1(rA), .in_2(ID_EX_RD), .rA(isequal5_1_ra));
  IsEqual5 isequal5_2 (.in_1(rA), .in_2(EX_MEM_rd), .rA(isequal5_2_ra));
  IsEqual5 isequal5_3 (.in_1(rA), .in_2(MEM_WB_rd), .rA(isequal5_3_ra));
  or or_2 (or_2_out, rB[4], rB[3], rB[2], rB[1], rB[0]);
  IsEqual5 isequal5_4 (.in_1(rB), .in_2(EX_MEM_rd), .rA(isequal5_4_ra));
  IsEqual5 isequal5_5 (.in_1(rB), .in_2(MEM_WB_rd), .rA(isequal5_5_ra));
  IsEqual5 isequal5_6 (.in_1(ID_EX_RD), .in_2(rB), .rA(isequal5_6_ra));
  or or_3 (or_3_out, isequal5_2_ra, isequal5_1_ra, isequal5_3_ra);
  or or_4 (or_4_out, isequal5_4_ra, isequal5_6_ra, isequal5_5_ra);
  and and_1 (and_1_out, or_1_out, or_3_out);
  and and_2 (and_2_out, or_2_out, or_4_out);
  or or_5 (Hazard, and_2_out, and_1_out);
endmodule

// MDet
module Detect_Load_Use (
  input  [4:0] rA,
  input  [4:0] rB,
  input  [4:0] ID_EX_rT,
  input  ID_EX_MemRead,
  output Hazard
);

  wire and_1_out, and_2_out, isequal5_1_ra, isequal5_2_ra, or_1_out, or_2_out;

  or or_1 (or_1_out, rA[4], rA[3], rA[2], rA[1], rA[0]);
  and and_1 (and_1_out, or_1_out, ID_EX_MemRead, isequal5_1_ra);
  IsEqual5 isequal5_1 (.in_1(rA), .in_2(ID_EX_rT), .rA(isequal5_1_ra));
  or or_2 (or_2_out, rB[4], rB[3], rB[2], rB[1], rB[0]);
  IsEqual5 isequal5_2 (.in_1(rB), .in_2(ID_EX_rT), .rA(isequal5_2_ra));
  and and_2 (and_2_out, or_2_out, ID_EX_MemRead, isequal5_2_ra);
  or or_3 (Hazard, and_2_out, and_1_out);
endmodule

// Fwd
module Forwarding (
  input  [4:0] ID_Ex_Rb,
  input  Hazard,
  input  Ex_M_We,
  input  [4:0] Ex_M_Rd,
  input  [4:0] ID_Ex_Ra,
  input  M_WB_We,
  input  [4:0] M_WB_Rd,
  output [1:0] B,
  output [1:0] A
);

  wire and_1_out, and_2_out, and_3_out, and_4_out, and_5_out, and_6_out, and_7_out, and_8_out, and_9_out,
       and_10_out, and_11_out, and_12_out, isequal5_1_ra, isequal5_2_ra, isequal5_3_ra, isequal5_4_ra,
       nor_1_out, nor_2_out;

  IsEqual5 isequal5_1 (.in_1(M_WB_Rd), .in_2(ID_Ex_Rb), .rA(isequal5_1_ra));
  IsEqual5 isequal5_2 (.in_1(ID_Ex_Rb), .in_2(Ex_M_Rd), .rA(isequal5_2_ra));
  or or_1 (B[1], and_1_out, and_5_out);
  and and_1 (and_1_out, Hazard, and_3_out, ~and_8_out);  // AND_Gate
  buf and_2 (and_2_out, ~nor_1_out);  // AND_Gate AND_Gate
  nor nor_1 (nor_1_out, M_WB_Rd[0], M_WB_Rd[1], M_WB_Rd[2], M_WB_Rd[3], M_WB_Rd[4]);
  and and_3 (and_3_out, isequal5_2_ra, and_4_out);
  buf and_4 (and_4_out, ~nor_2_out);  // AND_Gate AND_Gate
  nor nor_2 (nor_2_out, Ex_M_Rd[0], Ex_M_Rd[1], Ex_M_Rd[2], Ex_M_Rd[3], Ex_M_Rd[4]);
  IsEqual5 isequal5_3 (.in_1(ID_Ex_Ra), .in_2(M_WB_Rd), .rA(isequal5_3_ra));
  or or_2 (B[0], and_6_out, and_5_out);
  and and_5 (and_5_out, and_3_out, Hazard, and_8_out);
  and and_6 (and_6_out, ~and_3_out, Hazard, and_8_out);  // AND_Gate
  and and_7 (and_7_out, isequal5_3_ra, and_2_out);
  and and_8 (and_8_out, and_2_out, isequal5_1_ra);
  or or_3 (A[1], and_9_out, and_12_out);
  and and_9 (and_9_out, and_10_out, Hazard, ~and_7_out);  // AND_Gate
  and and_10 (and_10_out, and_4_out, isequal5_4_ra);
  IsEqual5 isequal5_4 (.in_1(Ex_M_Rd), .in_2(ID_Ex_Ra), .rA(isequal5_4_ra));
  and and_11 (and_11_out, ~and_10_out, Hazard, and_7_out);  // AND_Gate
  or or_4 (A[0], and_11_out, and_12_out);
  and and_12 (and_12_out, and_10_out, Hazard, and_7_out);
endmodule

// Decoder
module Control_Decoder (
  input  [5:0] func,
  input  [5:0] Op,
  input  [4:0] rt,
  output RegDst,
  output RegWr,
  output ALUSrc,
  output ALUOp1,
  output ALUOp0,
  output [3:0] MemData,
  output MemToReg
);

  wire and_1_out, and_2_out, and_3_out, and_4_out, and_6_out, and_7_out, and_8_out, and_9_out, and_10_out,
       and_11_out, and_12_out, and_13_out, and_14_out, and_15_out, and_16_out, and_17_out, and_18_out,
       jr_jalr_detect, nand_1_out, or_4_out;

  and and_1 (and_1_out, ~func[1], ~func[2], func[3], ~func[4], ~func[5]);  // AND_Gate
  and and_2 (and_2_out, ~rt[1], ~rt[2]);  // AND_Gate
  and and_3 (and_3_out, ~rt[3], ~rt[4]);  // AND_Gate
  and and_4 (and_4_out, and_6_out, Op[0]);
  and and_5 (jr_jalr_detect, and_1_out, and_18_out);
  and and_6 (and_6_out, ~Op[3], ~Op[4], ~Op[5]);  // AND_Gate
  nand nand_1 (nand_1_out, Op[0], Op[1], Op[2]);
  and and_7 (and_7_out, Op[3], ~Op[4], ~Op[5]);  // AND_Gate
  and and_8 (and_8_out, ~Op[4], Op[5]);  // AND_Gate
  and and_9 (and_9_out, ~Op[2], Op[1], Op[0]);  // AND_Gate
  and and_10 (and_10_out, and_2_out, and_4_out, and_3_out);
  and and_11 (and_11_out, nand_1_out, and_7_out);
  and and_12 (and_12_out, and_6_out, Op[2]);
  and and_13 (and_13_out, Op[0], Op[1], Op[2], Op[3]);
  and and_14 (and_14_out, ~Op[0], ~Op[1], ~Op[2]);  // AND_Gate
  and and_15 (and_15_out, Op[1], ~Op[2]);  // AND_Gate
  and and_16 (and_16_out, and_8_out, and_9_out);
  or or_1 (ALUOp0, and_12_out, and_10_out);
  and and_17 (and_17_out, and_6_out, and_15_out);
  and and_18 (and_18_out, and_6_out, and_14_out);
  or or_2 (ALUOp1, and_18_out, and_13_out, and_11_out);
  or or_3 (ALUSrc, and_7_out, and_16_out, and_8_out);
  and and_19 (MemData[0], and_8_out, ~Op[3]);  // AND_Gate
  and and_20 (MemData[3], and_8_out, Op[3]);
  or or_4 (or_4_out, ALUOp1, MemData[0]);
  and and_21 (RegWr, ~and_17_out, or_4_out, ~ALUOp0, ~jr_jalr_detect);  // AND_Gate
  not not_1 (RegDst, and_18_out);

  assign MemData[2:1] = {Op[0], Op[2]};
  assign MemToReg = MemData[0];

  // Notes on the sheet:
  //   signed?
  //   word?
  //   MemRead
  //   MemWrite
endmodule

// R Decoder
module ALUOpCoderRTypeInstruction (
  input  ALUOp1,
  input  ALUOp2,
  input  func5,
  input  func4,
  input  func3,
  input  func2,
  input  func1,
  input  func0,
  output op3,
  output op2,
  output op1,
  output op0,
  output movn,
  output movz,
  output shift_src,
  output JALR,
  output JR,
  output sltyes,
  output sltunsignedcheck
);

  wire and_3_out, and_4_out, and_5_out, and_6_out, and_7_out, and_8_out, and_9_out, and_10_out, and_11_out,
       and_12_out, and_13_out, and_14_out, and_15_out, not_1_out, not_2_out, not_3_out, not_4_out, not_5_out,
       not_6_out, not_7_out, not_8_out, not_9_out, not_10_out, not_11_out, not_12_out, not_13_out,
       not_14_out, not_15_out, not_16_out, not_17_out, not_18_out, or_2_out;

  and and_1 (op3, func5, func2);
  not not_1 (not_1_out, func3);
  and and_2 (op2, not_1_out, func1);
  not not_2 (not_2_out, ALUOp1);
  and and_3 (and_3_out, not_2_out, func3);
  and and_4 (and_4_out, func3, func1);
  and and_5 (and_5_out, func3, func2);
  and and_6 (and_6_out, func4, func3);
  and and_7 (and_7_out, func5, func0);
  and and_8 (and_8_out, func5, func3);
  and and_9 (and_9_out, ALUOp2, func3);
  not not_3 (not_3_out, ALUOp1);
  and and_10 (and_10_out, not_3_out, not_4_out, func0);
  not not_4 (not_4_out, func5);
  not not_5 (not_5_out, func5);
  and and_11 (and_11_out, not_5_out, not_6_out, func0);
  not not_6 (not_6_out, func3);
  not not_7 (not_7_out, func5);
  and and_12 (and_12_out, not_7_out, func1, func0);
  not not_8 (not_8_out, func5);
  and and_13 (and_13_out, not_8_out, func2);
  not not_9 (not_9_out, func5);
  and and_14 (and_14_out, not_9_out, func4, func0);
  and and_15 (and_15_out, ALUOp2, not_10_out, func0);
  not not_10 (not_10_out, func5);
  not not_11 (not_11_out, func5);
  not not_12 (not_12_out, func4);
  not not_13 (not_13_out, func2);
  not not_14 (not_14_out, func5);
  not not_15 (not_15_out, func4);
  not not_16 (not_16_out, func2);
  not not_17 (not_17_out, func0);
  and and_16 (JALR, func0, ~func1, ~func5, ~func4);  // AND_Gate
  and and_17 (JR, ~func4, ~func5, ~func1, func3, not_18_out);  // AND_Gate
  not not_18 (not_18_out, func0);
  and and_18 (sltyes, func5, ~func4, func3);  // AND_Gate
  and and_19 (movn, not_11_out, not_12_out, func3, not_13_out, func1, func0);
  and and_20 (movz, not_14_out, not_15_out, func3, not_16_out, func1, not_17_out);
  or or_1 (op1, and_3_out, and_4_out, and_5_out, and_6_out, and_7_out, and_8_out, and_9_out);
  or or_2 (or_2_out, and_10_out, and_11_out, and_12_out, and_13_out, and_14_out, and_15_out);
  and and_21 (op0, or_2_out, func0);
  and and_22 (sltunsignedcheck, sltyes, func0);

  assign shift_src = func2;
endmodule

// I Decoder
module ALUImmediateOPCircuit (
  input  bit5,
  input  bit4,
  input  bit3,
  input  bit2,
  input  bit1,
  input  bit0,
  input  [4:0] rt,
  input  aluOp0,
  input  aluOp1,
  output op3,
  output op2,
  output op1,
  output op0,
  output bltz,
  output bgez,
  output sltunsigned,
  output sltyes,
  output j,
  output jal,
  output beq,
  output bne,
  output blez,
  output bgtz,
  output LUI
);

  wire and_1_out, and_2_out, and_3_out, and_4_out, and_5_out, and_6_out, and_7_out, and_14_out, and_16_out,
       and_17_out, and_18_out, and_22_out, and_23_out, and_26_out, not_1_out, not_2_out, not_3_out,
       not_4_out, not_5_out, not_6_out, not_7_out, not_8_out, not_9_out, not_10_out, not_11_out, not_12_out,
       not_13_out, not_14_out, not_15_out, not_16_out, not_17_out, not_18_out, not_19_out, not_20_out,
       not_21_out, not_22_out, not_23_out, not_24_out, not_25_out, not_26_out, not_27_out, not_28_out,
       not_29_out;

  and and_1 (and_1_out, bit3, bit2, not_1_out);
  not not_1 (not_1_out, bit1);
  and and_2 (and_2_out, bit3, bit2, not_2_out);
  not not_2 (not_2_out, bit0);
  not not_3 (not_3_out, bit5);
  and and_3 (and_3_out, not_3_out, not_4_out, bit2);
  not not_4 (not_4_out, bit3);
  and and_4 (and_4_out, bit2, bit1, not_5_out);
  not not_5 (not_5_out, bit0);
  not not_6 (not_6_out, bit2);
  and and_5 (and_5_out, not_6_out, not_7_out);
  not not_7 (not_7_out, bit1);
  not not_8 (not_8_out, bit3);
  and and_6 (and_6_out, not_8_out, bit2);
  and and_7 (and_7_out, bit2, bit0);
  not not_9 (not_9_out, bit3);
  and and_8 (op0, not_9_out, bit2);
  not not_10 (not_10_out, bit5);
  not not_11 (not_11_out, bit2);
  not not_12 (not_12_out, bit5);
  not not_13 (not_13_out, bit2);
  not not_14 (not_14_out, bit3);
  not not_15 (not_15_out, bit2);
  not not_16 (not_16_out, bit0);
  not not_17 (not_17_out, bit5);
  not not_18 (not_18_out, bit3);
  not not_19 (not_19_out, bit2);
  not not_20 (not_20_out, bit5);
  not not_21 (not_21_out, bit3);
  not not_22 (not_22_out, bit1);
  not not_23 (not_23_out, bit0);
  not not_24 (not_24_out, bit5);
  not not_25 (not_25_out, bit3);
  not not_26 (not_26_out, bit1);
  not not_27 (not_27_out, bit3);
  not not_28 (not_28_out, bit0);
  not not_29 (not_29_out, bit3);
  and and_9 (LUI, bit0, bit1, bit2, bit3, ~bit4, ~bit5);  // AND_Gate
  or or_1 (op3, and_1_out, and_2_out);
  or or_2 (op2, and_3_out, and_4_out);
  or or_3 (op1, and_5_out, and_6_out, and_7_out, bit5);
  and and_10 (sltunsigned, not_10_out, bit3, not_11_out, bit1, bit0);
  and and_11 (sltyes, not_12_out, bit3, not_13_out, bit1);
  and and_12 (j, not_14_out, not_15_out, not_16_out, bit1);
  and and_13 (jal, not_17_out, not_18_out, bit1, not_19_out, bit0);
  and and_14 (and_14_out, not_20_out, not_21_out, not_22_out, not_23_out);
  and and_15 (beq, and_14_out, and_23_out);
  and and_16 (and_16_out, not_24_out, not_25_out, not_26_out, bit0);
  and and_17 (and_17_out, not_27_out, bit2, bit1, not_28_out);
  and and_18 (and_18_out, not_29_out, bit2, bit1, bit0);
  and and_19 (bne, and_23_out, and_16_out);
  and and_20 (blez, and_23_out, and_17_out);
  and and_21 (bgtz, and_23_out, and_18_out);
  and and_22 (and_22_out, ~bit3, ~bit1, ~bit2, bit0);  // AND_Gate
  and and_23 (and_23_out, ~aluOp1, aluOp0);  // AND_Gate
  and and_24 (bgez, and_22_out, rt[0]);
  and and_25 (bltz, and_22_out, and_26_out);
  and and_26 (and_26_out, ~rt[0], ~rt[1], ~rt[2], ~rt[3], ~rt[4]);  // AND_Gate
endmodule

// Jump
module Jumping (
  input  [31:0] A,
  input  jal,
  input  j,
  input  jr,
  input  jalr,
  input  [25:0] Inst,
  input  [31:0] PC_4,
  output [31:0] pcabs,
  output [31:0] PC_8,
  output jump,
  output link
);

  wire or_1_out, or_2_out;
  wire [27:0] bit_extender_1_out, shifter_1_out;
  wire [31:0] multiplexer_1_out;

  assign bit_extender_1_out = {{2{1'b0}}, Inst};  // Bit_Extender bit_extender_1
  Shifter #(.width(28)) shifter_1 (.in(bit_extender_1_out), .\dist (5'b00010), .out(shifter_1_out));
  or or_1 (or_1_out, jal, j);
  Multiplexer #(.width(32), .enable("false")) multiplexer_1 (
    .in0(PC_4), .in1({PC_4[31:28], shifter_1_out}), .out(multiplexer_1_out), .sel(or_1_out));
  or or_2 (or_2_out, jr, jalr);
  or or_3 (jump, or_1_out, or_2_out);
  Multiplexer #(.width(32), .enable("false")) multiplexer_2 (
    .in0(multiplexer_1_out), .in1(A), .out(pcabs), .sel(or_2_out));
  or or_4 (link, jal, jalr);
  // Incrementer incrementer_1: pin names not known; wires that end beside it: PC_4[31:2], PC_8[31:2]

  assign PC_8[1:0] = PC_4[1:0];

  // Notes on the sheet:
  //   +4
endmodule

// Branch
module Branching (
  input  bgtz,
  input  blez,
  input  bgez,
  input  bltz,
  input  beq,
  input  bne,
  input  [31:0] B,
  input  [31:0] A,
  input  [31:0] PC_4,
  input  [15:0] Imm,
  output [31:0] pcrel
);

  wire and_2_out, comparator_1_eq, comparator_1_gt, comparator_1_lt, multiplexer_1_out, multiplexer_2_out,
       or_1_out, or_2_out, or_3_out, or_4_out, xor_1_out, xor_2_out, xor_3_out;
  wire [29:0] incrementer_1_p2;
  wire [31:0] adder_1_out, and_1_out, bit_extender_1_out, bit_extender_2_out, shifter_1_out;

  assign bit_extender_1_out = {{16{1'b0}}, Imm};  // Bit_Extender bit_extender_1
  or or_1 (or_1_out, bgtz, blez, bgez, bltz);
  Shifter #(.width(32)) shifter_1 (.in(bit_extender_1_out), .\dist (5'b00010), .out(shifter_1_out));
  assign bit_extender_2_out = {{31{or_1_out}}, or_1_out};  // Bit_Extender bit_extender_2
  assign and_1_out = ~bit_extender_2_out & B;  // AND_Gate and_1, 32 bits wide
  Comparator #(.width(32)) comparator_1 (
    .a(A), .b(and_1_out), .gt(comparator_1_gt), .eq(comparator_1_eq), .lt(comparator_1_lt));
  or or_2 (or_2_out, bgtz, blez);
  Multiplexer #(.enable("false")) multiplexer_1 (
    .in0(comparator_1_eq), .in1(comparator_1_gt), .out(multiplexer_1_out), .sel(or_2_out));
  xor xor_1 (xor_1_out, blez, multiplexer_1_out);
  Adder #(.width(32)) adder_1 (.a(PC_4), .b(shifter_1_out), .out(adder_1_out));  // open: cin, cout
  or or_3 (or_3_out, bgez, bltz);
  Multiplexer #(.enable("false")) multiplexer_2 (
    .in0(xor_1_out), .in1(comparator_1_lt), .out(multiplexer_2_out), .sel(or_3_out));
  // Incrementer incrementer_1: pin names not known; wires that end beside it: PC_4[31:2], incrementer_1_p2
  xor xor_2 (xor_2_out, bgez, multiplexer_2_out);
  and and_2 (and_2_out, xor_2_out, or_4_out);
  xor xor_3 (xor_3_out, bne, and_2_out);
  or or_4 (or_4_out, beq, bne);
  Multiplexer #(.width(32), .enable("false")) multiplexer_3 (
    .in0({incrementer_1_p2, PC_4[1:0]}), .in1(adder_1_out), .out(pcrel), .sel(xor_3_out));

  // Notes on the sheet:
  //   +4
endmodule

// Load
module Loading (
  input  [31:0] A,
  input  lbu,
  input  [3:0] byte_word,
  output [31:0] B
);

  wire and_1_out, xor_1_out;
  wire [31:0] bit_extender_1_out;

  assign bit_extender_1_out = {{24{A[7]}}, A[7:0]};  // Bit_Extender bit_extender_1
  Multiplexer #(.width(32), .enable("false")) multiplexer_1 (
    .in0(A), .in1(bit_extender_1_out), .out(B), .sel(and_1_out));
  and and_1 (and_1_out, xor_1_out, ~lbu);  // AND_Gate
  ExactlyOne xor_1 (.out(xor_1_out), .in0(byte_word[3]), .in1(byte_word[2]), .in2(byte_word[1]), .in3(byte_word[0]));
endmodule

// ==
module IsEqual5 (
  input  [4:0] in_1,
  input  [4:0] in_2,
  output rA
);

  wire [4:0] xnor_1_out;

  assign xnor_1_out = ~(in_1 ^ in_2);  // XNOR_Gate xnor_1, 5 bits wide
  and and_1 (rA, xnor_1_out[0], xnor_1_out[1], xnor_1_out[2], xnor_1_out[3], xnor_1_out[4]);
endmodule

// ==0
module IsZero32 (
  input  [31:0] In,
  output Out
);

  nor nor_1 (Out, In[0], In[1], In[2], In[3], In[4], In[5], In[6], In[7], In[8], In[9], In[10], In[11], In[12], In[13], In[14], In[15], In[16], In[17], In[18], In[19], In[20], In[21], In[22], In[23], In[24], In[25], In[26], In[27], In[28], In[29], In[30], In[31]);
endmodule

// <<0x
module ByteShift (
  input  [31:0] B,
  input  sign,
  input  [3:0] Sa,
  output [31:0] C
);

  wire and_1_out, and_2_out, and_3_out, and_4_out;
  wire [31:0] byteshift1_1_c, byteshift2_1_c, byteshift3_1_c, multiplexer_1_out, multiplexer_2_out;

  and and_1 (and_1_out, Sa[0], Sa[3], Sa[2], Sa[1]);
  Multiplexer #(.width(32), .enable("false")) multiplexer_1 (
    .in0(B), .in1(byteshift3_1_c), .out(multiplexer_1_out), .sel(and_2_out));
  ByteShift3 byteshift3_1 (.Cin(sign), .B(B), .C(byteshift3_1_c));
  and and_2 (and_2_out, ~and_1_out, Sa[3]);  // AND_Gate
  ByteShift2 byteshift2_1 (.Cin(sign), .B(multiplexer_1_out), .C(byteshift2_1_c));
  and and_3 (and_3_out, ~and_1_out, Sa[2]);  // AND_Gate
  Multiplexer #(.width(32), .enable("false")) multiplexer_2 (
    .in0(multiplexer_1_out), .in1(byteshift2_1_c), .out(multiplexer_2_out), .sel(and_3_out));
  ByteShift1 byteshift1_1 (.Cin(sign), .B(multiplexer_2_out), .C(byteshift1_1_c));
  Multiplexer #(.width(32), .enable("false")) multiplexer_3 (
    .in0(multiplexer_2_out), .in1(byteshift1_1_c), .out(C), .sel(and_4_out));
  and and_4 (and_4_out, ~and_1_out, Sa[1]);  // AND_Gate
endmodule

// >>0x
module ByteShiftRight (
  input  [31:0] B,
  input  [3:0] Sa,
  input  sign,
  output [31:0] C
);

  ByteShift byteshift_1 (
    .B({B[0], B[1], B[2], B[3], B[4], B[5], B[6], B[7], B[8], B[9], B[10], B[11], B[12], B[13], B[14], B[15], B[16], B[17], B[18], B[19], B[20], B[21], B[22], B[23], B[24], B[25], B[26], B[27], B[28], B[29], B[30], B[31]}),
    .Sa(Sa), .sign(sign),
    .C({C[0], C[1], C[2], C[3], C[4], C[5], C[6], C[7], C[8], C[9], C[10], C[11], C[12], C[13], C[14], C[15], C[16], C[17], C[18], C[19], C[20], C[21], C[22], C[23], C[24], C[25], C[26], C[27], C[28], C[29], C[30], C[31]}));
endmodule

// <<1
module ByteShift1 (
  input  Cin,
  input  [31:0] B,
  output [31:0] C
);

  assign C[7:0] = {{7{Cin}}, Cin};  // Bit_Extender bit_extender_1
  Bit_Extender #(.in_width(32), .out_width(24)) bit_extender_2 (.in(B), .out(C[31:8]));
endmodule

// <<2
module ByteShift2 (
  input  Cin,
  input  [31:0] B,
  output [31:0] C
);

  assign C[15:0] = {{15{Cin}}, Cin};  // Bit_Extender bit_extender_1
  Bit_Extender #(.in_width(32)) bit_extender_2 (.in(B), .out(C[31:16]));
endmodule

// <<3
module ByteShift3 (
  input  Cin,
  input  [31:0] B,
  output [31:0] C
);

  assign C[23:0] = {{23{Cin}}, Cin};  // Bit_Extender bit_extender_1
  Bit_Extender #(.in_width(32), .out_width(8)) bit_extender_2 (.in(B), .out(C[31:24]));
endmodule

module IDForwarding (
  input  Hazard,
  input  EX_M__rB,
  input  M_WB__rB,
  input  EX_M__rA,
  input  M_WB__rA,
  output [1:0] B,
  output [1:0] A
);

  wire not_2_out, not_3_out;

  not not_1 (A[1], Hazard);
  not not_2 (not_2_out, EX_M__rB);
  not not_3 (not_3_out, EX_M__rA);
  and and_1 (B[0], not_2_out, M_WB__rB);
  and and_2 (A[0], not_3_out, M_WB__rA);

  assign B[1] = A[1];
endmodule

module IDetect_Hazard (
  input  [4:0] rA,
  input  [4:0] rB,
  input  [4:0] EX_MEM_rd,
  input  [4:0] MEM_WB_rd,
  output Hazard,
  output EX_M__rB,
  output M_WB__rB,
  output EX_M__rA,
  output M_WB__rA
);

  wire and_1_out, and_2_out, or_1_out, or_2_out, or_3_out, or_4_out;

  or or_1 (or_1_out, rA[4], rA[3], rA[2], rA[1], rA[0]);
  IsEqual5 isequal5_1 (.in_1(rA), .in_2(EX_MEM_rd), .rA(EX_M__rA));
  IsEqual5 isequal5_2 (.in_1(rA), .in_2(MEM_WB_rd), .rA(M_WB__rA));
  or or_2 (or_2_out, rB[4], rB[3], rB[2], rB[1], rB[0]);
  IsEqual5 isequal5_3 (.in_1(rB), .in_2(EX_MEM_rd), .rA(EX_M__rB));
  IsEqual5 isequal5_4 (.in_1(rB), .in_2(MEM_WB_rd), .rA(M_WB__rB));
  or or_3 (or_3_out, EX_M__rA, M_WB__rA);
  or or_4 (or_4_out, EX_M__rB, M_WB__rB);
  and and_1 (and_1_out, or_1_out, or_3_out);
  and and_2 (and_2_out, or_2_out, or_4_out);
  or or_5 (Hazard, and_2_out, and_1_out);

  // Other names for the same wires on the sheet: EX_MEM[4:0] = EX_MEM_rd; MEM_WB[4:0] = MEM_WB_rd
endmodule
