// Logisim project MIPS_pipeline2.circ as structural Verilog: 9 circuits, main circuit MIPS32
module MIPS32 (
);

  wire ALUSrc_q, and_1_out, and_2_out, and_4_out, and_5_out, Clk, control_decoder_1_aluop0,
       control_decoder_1_aluop1, control_decoder_1_alusrc, control_decoder_1_regdst, control_decoder_1_regwr,
       detect_hazard_1_hazard, ex_1_writeenable, EX_Mem_WE, Haz_Fwd_q, M_WB_WE, MovE, Move_Enable_2_q,
       Move_Enable_3_q, Move_Enable_q, multiplexer_1_out, not_1_out, WB_Ctrl, WB_Ctrl_2_q, WB_Ctrl_3_q,
       WB_Ctrl_q;
  wire [1:0] aluimmediateopcircuit_1_sltyes, aluopcoderrtypeinstruction_1_movz,
       aluopcoderrtypeinstruction_1_sltyes, forwarding_1_a, forwarding_1_b, mov_controls_q,
       multiplexer_4_out, register_1_q, slt_controls_q;
  wire [3:0] aluimmediateopcircuit_1_op0, ALUOpCode_q, aluopcoderrtypeinstruction_1_op0, bit_extender_1_out,
       multiplexer_2_out, multiplexer_8_out;
  wire [4:0] ID_EX_Ra, ID_EX_Rb, ID_EX_Rd, MRD, multiplexer_5_out, rA, rB, registerfile_1_p4, rW, RW_2_q,
       RW_q, WRD;
  wire [4:4] aluimmediateopcircuit_1_lui;
  wire [5:0] aluopcoderrtypeinstruction_1_shift_src, Inst_q, SHAMT_src_q;
  wire [29:0] incrementer_1_p1, incrementer_1_p2;
  wire [31:0] A_q, ALU_Out_2_q, ALU_Out_q, B_q, bit_extender_2_out, bit_extender_3_out, ex_1_b_2, ex_1_d,
       Imm_q, Memory_Out_2_q, Memory_Out_q, mips_ram_1_p4, mipsprogramrom_1_p1, multiplexer_7_out,
       multiplexer_9_out, multiplexer_10_out, PC_4_2_q, PC_4_q, registerfile_1_p1, registerfile_1_p7,
       registerfile_1_p8;
  wire [31:6] Inst_q_2;

  Clock clock_1 (.out(Clk));
  // Incrementer incrementer_1: pin names not known; wires that end beside it: incrementer_1_p1, incrementer_1_p2
  Register #(.width(32)) register_1 (
    .D({incrementer_1_p2, register_1_q}), .Q({incrementer_1_p1, register_1_q}), .clk(Clk));  // open: en, clr
  // MIPSProgramROM mipsprogramrom_1: pin names not known; wires that end beside it: mipsprogramrom_1_p1
  Register #(.width(32)) Inst (
    .D(mipsprogramrom_1_p1), .Q({Inst_q_2[31:26], rA, rB, Inst_q_2[15:6], Inst_q}), .clk(Clk));  // open: en, clr
  Register #(.width(32)) PC_4 (.D({incrementer_1_p1, register_1_q}), .Q(PC_4_q), .clk(Clk));  // open: en, clr
  and and_1 (and_1_out, ~Inst_q[5], ~Inst_q[4], Inst_q[3], Inst_q[1]);  // AND_Gate
  and and_2 (and_2_out, ~Inst_q_2[31], ~Inst_q_2[30], ~Inst_q_2[29], ~Inst_q_2[27], ~Inst_q_2[26], ~Inst_q_2[28]);  // AND_Gate
  and and_3 (MovE, and_1_out, ~control_decoder_1_alusrc);  // AND_Gate
  Control_Decoder control_decoder_1 (
    .func(Inst_q), .Op(Inst_q_2[31:26]), .rt(rB), .RegDst(control_decoder_1_regdst),
    .RegWr(control_decoder_1_regwr), .ALUSrc(control_decoder_1_alusrc), .ALUOp1(control_decoder_1_aluop1),
    .ALUOp0(control_decoder_1_aluop0), .MemToReg(WB_Ctrl));  // open: MemRead, MemWrite
  Multiplexer #(.enable("false")) multiplexer_1 (
    .in0(control_decoder_1_regwr), .in1(M_WB_WE), .out(multiplexer_1_out), .sel(Move_Enable_3_q));
  ALUImmediateOPCircuit aluimmediateopcircuit_1 (
    .bit5(Inst_q_2[31]), .bit4(Inst_q_2[30]), .bit3(Inst_q_2[29]), .bit2(Inst_q_2[28]), .bit1(Inst_q_2[27]),
    .bit0(Inst_q_2[26]), .rt(rB), .aluOp1(control_decoder_1_aluop1), .aluOp0(control_decoder_1_aluop0),
    .op3(aluimmediateopcircuit_1_op0[3]), .op2(aluimmediateopcircuit_1_op0[2]),
    .op1(aluimmediateopcircuit_1_op0[1]), .op0(aluimmediateopcircuit_1_op0[0]),
    .sltunsigned(aluimmediateopcircuit_1_sltyes[1]), .sltyes(aluimmediateopcircuit_1_sltyes[0]),
    .LUI(aluimmediateopcircuit_1_lui[4]));  // open: bltz, bgez, j, jal, beq, bne, blez, bgtz
  Multiplexer #(.width(4), .enable("false")) multiplexer_2 (
    .in0(aluimmediateopcircuit_1_op0), .in1(bit_extender_1_out), .out(multiplexer_2_out),
    .sel(aluimmediateopcircuit_1_lui[4]));
  not not_1 (not_1_out, aluimmediateopcircuit_1_lui[4]);
  assign bit_extender_1_out = {{3{not_1_out}}, not_1_out};  // Bit_Extender bit_extender_1
  Multiplexer #(.width(5), .enable("false")) multiplexer_3 (
    .in0(Inst_q_2[15:11]), .in1(rB), .out(rW), .sel(control_decoder_1_regdst));
  ALUOpCoderRTypeInstruction aluopcoderrtypeinstruction_1 (
    .ALUOp1(control_decoder_1_aluop1), .ALUOp2(control_decoder_1_aluop0), .func5(Inst_q[5]),
    .func4(Inst_q[4]), .func3(Inst_q[3]), .func2(Inst_q[2]), .func1(Inst_q[1]), .func0(Inst_q[0]),
    .op3(aluopcoderrtypeinstruction_1_op0[3]), .op2(aluopcoderrtypeinstruction_1_op0[2]),
    .op1(aluopcoderrtypeinstruction_1_op0[1]), .op0(aluopcoderrtypeinstruction_1_op0[0]),
    .movn(aluopcoderrtypeinstruction_1_movz[1]), .movz(aluopcoderrtypeinstruction_1_movz[0]),
    .shift_src(aluopcoderrtypeinstruction_1_shift_src[0]), .sltyes(aluopcoderrtypeinstruction_1_sltyes[0]),
    .sltunsignedcheck(aluopcoderrtypeinstruction_1_sltyes[1]));  // open: JALR, JR
  Multiplexer #(.width(2), .enable("false")) multiplexer_4 (
    .in0(aluimmediateopcircuit_1_sltyes), .in1(aluopcoderrtypeinstruction_1_sltyes), .out(multiplexer_4_out),
    .sel(and_2_out));
  Multiplexer #(.width(5), .enable("false")) multiplexer_5 (
    .in0(Inst_q_2[10:6]), .in1(rA), .out(multiplexer_5_out), .sel(and_4_out));
  and and_4 (and_4_out, ~Inst_q[5], ~Inst_q[4], Inst_q[2], ~Inst_q[3]);  // AND_Gate
  // RegisterFile registerfile_1: pin names not known; wires that end beside it: registerfile_1_p1, Clk, multiplexer_1_out, registerfile_1_p4, rA, rB, registerfile_1_p7, registerfile_1_p8
  Detect_Hazard detect_hazard_1 (
    .ID_EX_RD(ID_EX_Rd), .EX_MEM_rd(WRD), .MEM_WB_rd(MRD), .rA(rA), .rB(rB), .Hazard(detect_hazard_1_hazard));
  assign bit_extender_2_out = {{16{Inst_q_2[15]}}, {Inst_q_2[15:6], Inst_q}};  // Bit_Extender bit_extender_2
  assign bit_extender_3_out = {{16{1'b0}}, {Inst_q_2[15:6], Inst_q}};  // Bit_Extender bit_extender_3
  Multiplexer #(.width(5), .enable("false")) multiplexer_6 (
    .in0(multiplexer_5_out), .in1({aluimmediateopcircuit_1_lui[4], bit_extender_1_out}),
    .out(aluopcoderrtypeinstruction_1_shift_src[5:1]), .sel(aluimmediateopcircuit_1_lui[4]));
  Multiplexer #(.width(32), .enable("false")) multiplexer_7 (
    .in0(bit_extender_2_out), .in1(bit_extender_3_out), .out(multiplexer_7_out), .sel(and_5_out));
  and and_5 (and_5_out, multiplexer_8_out[3], ~multiplexer_8_out[0]);  // AND_Gate
  Multiplexer #(.width(4), .enable("false")) multiplexer_8 (
    .in0(multiplexer_2_out), .in1(aluopcoderrtypeinstruction_1_op0), .out(multiplexer_8_out), .sel(and_2_out));
  Register #(.width(32)) A (.D(registerfile_1_p7), .Q(A_q), .clk(Clk));  // open: en, clr
  Register #(.width(32)) B (.D(registerfile_1_p8), .Q(B_q), .clk(Clk));  // open: en, clr
  Register #(.width(5)) RD_Ctrl (.D(rW), .Q(ID_EX_Rd), .clk(Clk));  // open: en, clr
  Register #(.width(32)) Imm (.D(multiplexer_7_out), .Q(Imm_q), .clk(Clk));  // open: en, clr
  Register #(.width(1)) ALUSrc (.D(control_decoder_1_alusrc), .Q(ALUSrc_q), .clk(Clk));  // open: en, clr
  Register #(.width(2)) mov_controls (
    .D(aluopcoderrtypeinstruction_1_movz), .Q(mov_controls_q), .clk(Clk));  // open: en, clr
  Register #(.width(4)) ALUOpCode (.D(multiplexer_8_out), .Q(ALUOpCode_q), .clk(Clk));  // open: en, clr
  Register #(.width(6)) SHAMT_src (
    .D(aluopcoderrtypeinstruction_1_shift_src), .Q(SHAMT_src_q), .clk(Clk));  // open: en, clr
  Register #(.width(2)) slt_controls (.D(multiplexer_4_out), .Q(slt_controls_q), .clk(Clk));  // open: en, clr
  Register #(.width(5)) u_RW (.D(rW), .Q(RW_q), .clk(Clk));  // open: en, clr
  Register #(.width(32)) PC_4_2 (.D(PC_4_q), .Q(PC_4_2_q), .clk(Clk));  // open: en, clr
  Register #(.width(1)) Move_Enable (.D(MovE), .Q(Move_Enable_q), .clk(Clk));  // open: en, clr
  Register #(.width(1)) u_WB_Ctrl (.D(WB_Ctrl), .Q(WB_Ctrl_q), .clk(Clk));  // open: en, clr
  Register #(.width(1)) Haz_Fwd (.D(detect_hazard_1_hazard), .Q(Haz_Fwd_q), .clk(Clk));  // open: en, clr
  Register #(.width(5)) u_Ra (.D(rA), .Q(ID_EX_Ra), .clk(Clk));  // open: en, clr
  Register #(.width(5)) u_Rb (.D(rB), .Q(ID_EX_Rb), .clk(Clk));  // open: en, clr
  Multiplexer #(.select(2), .width(32), .enable("false")) multiplexer_9 (
    .in0(A_q), .in1(registerfile_1_p1), .in2(ALU_Out_q), .in3(ALU_Out_q), .out(multiplexer_9_out),
    .sel(forwarding_1_a));
  Multiplexer #(.select(2), .width(32), .enable("false")) multiplexer_10 (
    .in0(B_q), .in1(registerfile_1_p1), .in2(ALU_Out_q), .in3(ALU_Out_q), .out(multiplexer_10_out),
    .sel(forwarding_1_b));
  Forwarding forwarding_1 (
    .ID_Ex_Rb(ID_EX_Rb), .Hazard(Haz_Fwd_q), .Ex_M_We(EX_Mem_WE), .Ex_M_Rd(MRD), .ID_Ex_Ra(ID_EX_Ra),
    .M_WB_We(M_WB_WE), .M_WB_Rd(WRD), .B(forwarding_1_b), .A(forwarding_1_a));
  EX ex_1 (
    .A(multiplexer_9_out), .B(multiplexer_10_out), .Imm(Imm_q), .ALUSrc(ALUSrc_q), .MOV(mov_controls_q),
    .ALUOpCode(ALUOpCode_q), .Shamt(SHAMT_src_q), .SLT(slt_controls_q), .PC_4(PC_4_2_q), .D(ex_1_d),
    .B_2(ex_1_b_2), .WriteEnable(ex_1_writeenable));
  Register #(.width(5)) RD_Ctrl_2 (.D(ID_EX_Rd), .Q(MRD), .clk(Clk));  // open: en, clr
  Register #(.width(32)) ALU_Out (.D(ex_1_d), .Q(ALU_Out_q), .clk(Clk));  // open: en, clr
  Register #(.width(32)) Memory_Out (.D(ex_1_b_2), .Q(Memory_Out_q), .clk(Clk));  // open: en, clr
  Register #(.width(1)) Write_Enable (.D(ex_1_writeenable), .Q(EX_Mem_WE), .clk(Clk));  // open: en, clr
  Register #(.width(5)) RW_2 (.D(RW_q), .Q(RW_2_q), .clk(Clk));  // open: en, clr
  Register #(.width(1)) Move_Enable_2 (.D(Move_Enable_q), .Q(Move_Enable_2_q), .clk(Clk));  // open: en, clr
  Register #(.width(1)) WB_Ctrl_2 (.D(WB_Ctrl_q), .Q(WB_Ctrl_2_q), .clk(Clk));  // open: en, clr
  // MIPS_RAM mips_ram_1: pin names not known; wires that end beside it: ALU_Out_q[19:0], Memory_Out_q, Clk, mips_ram_1_p4
  Register #(.width(5)) RD_Ctrl_3 (.D(MRD), .Q(WRD), .clk(Clk));  // open: en, clr
  Register #(.width(32)) ALU_Out_2 (.D(ALU_Out_q), .Q(ALU_Out_2_q), .clk(Clk));  // open: en, clr
  Register #(.width(32)) Memory_Out_2 (.D(mips_ram_1_p4), .Q(Memory_Out_2_q), .clk(Clk));  // open: en, clr
  Register #(.width(1)) Write_Enable_2 (.D(EX_Mem_WE), .Q(M_WB_WE), .clk(Clk));  // open: en, clr
  Register #(.width(5)) RW_3 (.D(RW_2_q), .Q(registerfile_1_p4), .clk(Clk));  // open: en, clr
  Register #(.width(1)) Move_Enable_3 (.D(Move_Enable_2_q), .Q(Move_Enable_3_q), .clk(Clk));  // open: en, clr
  Register #(.width(1)) WB_Ctrl_3 (.D(WB_Ctrl_2_q), .Q(WB_Ctrl_3_q), .clk(Clk));  // open: en, clr
  Multiplexer #(.width(32), .enable("false")) multiplexer_11 (
    .in0(ALU_Out_2_q), .in1(Memory_Out_2_q), .out(registerfile_1_p1), .sel(WB_Ctrl_3_q));

  // Notes on the sheet:
  //   +4
  //   IF/ID
  //   ID
  //   ID/EX
  //   Forwarding
  //   EX/MEM
  //   To Decode Stage
  //   MEM
  //   MEM/WB
  //   WB
endmodule

module EX (
  input  [31:0] A,
  input  [31:0] B,
  input  [31:0] Imm,
  input  ALUSrc,
  input  [1:0] MOV,
  input  [3:0] ALUOpCode,
  input  [5:0] Shamt,
  input  [1:0] SLT,
  input  [31:0] PC_4,
  output [31:0] D,
  output [31:0] B_2,
  output WriteEnable
);

  wire and_1_out, and_2_out, comparator_1_lt, comparator_2_lt, iszero32_1_out, iszero32_2_out,
       multiplexer_4_out, or_1_out, xor_1_out;
  wire [4:0] bit_extender_2_out, mips_alu_1_p5;
  wire [31:0] bit_extender_1_out, bit_extender_3_out, mips_alu_1_p6, multiplexer_1_out, multiplexer_2_out;

  Multiplexer #(.width(32), .enable("false")) multiplexer_1 (.in0(B), .in1(Imm), .out(multiplexer_1_out), .sel(ALUSrc));
  IsZero32 iszero32_1 (.In(multiplexer_1_out), .Out(iszero32_1_out));
  IsZero32 iszero32_2 (.In(multiplexer_1_out), .Out(iszero32_2_out));
  xor xor_1 (xor_1_out, MOV[0], MOV[1]);
  and and_1 (and_1_out, ~iszero32_1_out, MOV[0]);  // AND_Gate
  and and_2 (and_2_out, iszero32_2_out, MOV[1]);
  Multiplexer #(.width(32), .enable("false")) multiplexer_2 (
    .in0(multiplexer_1_out), .in1(bit_extender_1_out), .out(multiplexer_2_out), .sel(xor_1_out));
  assign bit_extender_1_out = {{31{1'b0}}, ALUSrc};  // Bit_Extender bit_extender_1
  or or_1 (or_1_out, and_1_out, and_2_out);
  Comparator #(.width(32)) comparator_1 (.a(A), .b(multiplexer_1_out), .lt(comparator_1_lt));  // open: gt, eq
  Comparator #(.width(32), .mode("unsigned")) comparator_2 (
    .a(A), .b(multiplexer_1_out), .lt(comparator_2_lt));  // open: gt, eq
  // Mips_ALU mips_alu_1: pin names not known; wires that end beside it: A, multiplexer_2_out, ALUOpCode, SLT[1], mips_alu_1_p5, mips_alu_1_p6
  Multiplexer #(.width(5), .enable("false")) multiplexer_3 (
    .in0(Shamt[5:1]), .in1(bit_extender_2_out), .out(mips_alu_1_p5), .sel(Shamt[0]));
  Bit_Extender #(.in_width(32), .out_width(5), .\type ("sign")) bit_extender_2 (.in(A), .out(bit_extender_2_out));
  Multiplexer #(.enable("false")) multiplexer_4 (
    .in0(comparator_1_lt), .in1(comparator_2_lt), .out(multiplexer_4_out), .sel(SLT[1]));
  assign bit_extender_3_out = {{31{1'b0}}, multiplexer_4_out};  // Bit_Extender bit_extender_3
  Multiplexer #(.width(32), .enable("false")) multiplexer_5 (
    .in0(mips_alu_1_p6), .in1(bit_extender_3_out), .out(D), .sel(SLT[0]));
  not not_1 (WriteEnable, or_1_out);

  assign B_2 = B;

  // Notes on the sheet:
  //   MOV
  //   SLT
endmodule

// Det
module Detect_Hazard (
  input  [4:0] rA,
  input  [4:0] rB,
  input  [4:0] ID_EX_RD,
  input  [4:0] EX_MEM_rd,
  input  [4:0] MEM_WB_rd,
  output Hazard
);

  wire and_1_out, and_2_out, isequal5_1_ra, isequal5_2_ra, isequal5_3_ra, isequal5_4_ra, isequal5_5_ra,
       isequal5_6_ra, or_1_out, or_2_out, or_3_out, or_4_out;

  or or_1 (or_1_out, rA[4], rA[3], rA[2], rA[1], rA[0]);
  IsEqual5 isequal5_1 (.in_1(rA), .in_2(ID_EX_RD), .rA(isequal5_1_ra));
  IsEqual5 isequal5_2 (.in_1(rA), .in_2(EX_MEM_rd), .rA(isequal5_2_ra));
  IsEqual5 isequal5_3 (.in_1(rA), .in_2(MEM_WB_rd), .rA(isequal5_3_ra));
  or or_2 (or_2_out, rB[4], rB[3], rB[2], rB[1], rB[0]);
  IsEqual5 isequal5_4 (.in_1(rB), .in_2(EX_MEM_rd), .rA(isequal5_4_ra));
  IsEqual5 isequal5_5 (.in_1(rB), .in_2(MEM_WB_rd), .rA(isequal5_5_ra));
  IsEqual5 isequal5_6 (.in_1(ID_EX_RD), .in_2(rB), .rA(isequal5_6_ra));
  or or_3 (or_3_out, isequal5_2_ra, isequal5_1_ra, isequal5_3_ra);
  or or_4 (or_4_out, isequal5_4_ra, isequal5_6_ra, isequal5_5_ra);
  and and_1 (and_1_out, or_1_out, or_3_out);
  and and_2 (and_2_out, or_2_out, or_4_out);
  or or_5 (Hazard, and_2_out, and_1_out);
endmodule

// Fwd
module Forwarding (
  input  [4:0] ID_Ex_Rb,
  input  Hazard,
  input  Ex_M_We,
  input  [4:0] Ex_M_Rd,
  input  [4:0] ID_Ex_Ra,
  input  M_WB_We,
  input  [4:0] M_WB_Rd,
  output [1:0] B,
  output [1:0] A
);

  wire and_1_out, and_2_out, and_3_out, and_4_out, and_5_out, and_6_out, and_7_out, and_8_out, and_9_out,
       and_10_out, and_11_out, and_12_out, isequal5_1_ra, isequal5_2_ra, isequal5_3_ra, isequal5_4_ra,
       nor_1_out, nor_2_out;

  IsEqual5 isequal5_1 (.in_1(M_WB_Rd), .in_2(ID_Ex_Rb), .rA(isequal5_1_ra));
  IsEqual5 isequal5_2 (.in_1(ID_Ex_Rb), .in_2(Ex_M_Rd), .rA(isequal5_2_ra));
  or or_1 (B[1], and_1_out, and_6_out);
  and and_1 (and_1_out, Hazard, and_3_out, ~and_8_out);  // AND_Gate
  and and_2 (and_2_out, M_WB_We, ~nor_1_out);  // AND_Gate
  nor nor_1 (nor_1_out, M_WB_Rd[0], M_WB_Rd[1], M_WB_Rd[2], M_WB_Rd[3], M_WB_Rd[4]);
  and and_3 (and_3_out, isequal5_2_ra, and_4_out);
  and and_4 (and_4_out, Ex_M_We, ~nor_2_out);  // AND_Gate
  nor nor_2 (nor_2_out, Ex_M_Rd[0], Ex_M_Rd[1], Ex_M_Rd[2], Ex_M_Rd[3], Ex_M_Rd[4]);
  IsEqual5 isequal5_3 (.in_1(ID_Ex_Ra), .in_2(M_WB_Rd), .rA(isequal5_3_ra));
  or or_2 (B[0], and_5_out, and_6_out);
  and and_5 (and_5_out, ~and_3_out, Hazard, and_8_out);  // AND_Gate
  and and_6 (and_6_out, and_3_out, Hazard, and_8_out);
  and and_7 (and_7_out, isequal5_3_ra, and_2_out);
  and and_8 (and_8_out, and_2_out, isequal5_1_ra);
  or or_3 (A[1], and_9_out, and_12_out);
  and and_9 (and_9_out, and_10_out, Hazard, ~and_7_out);  // AND_Gate
  and and_10 (and_10_out, and_4_out, isequal5_4_ra);
  IsEqual5 isequal5_4 (.in_1(Ex_M_Rd), .in_2(ID_Ex_Ra), .rA(isequal5_4_ra));
  and and_11 (and_11_out, ~and_10_out, Hazard, and_7_out);  // AND_Gate
  or or_4 (A[0], and_11_out, and_12_out);
  and and_12 (and_12_out, and_10_out, Hazard, and_7_out);
endmodule

// Decoder
module Control_Decoder (
  input  [5:0] func,
  input  [5:0] Op,
  input  [4:0] rt,
  output RegDst,
  output RegWr,
  output ALUSrc,
  output ALUOp1,
  output ALUOp0,
  output MemRead,
  output MemWrite,
  output MemToReg
);

  wire and_1_out, and_2_out, and_3_out, and_4_out, and_6_out, and_7_out, and_8_out, and_9_out, and_10_out,
       and_11_out, and_12_out, and_13_out, and_14_out, and_15_out, and_16_out, and_17_out, and_18_out,
       jr_jalr_detect, nand_1_out, or_4_out;

  and and_1 (and_1_out, ~func[1], ~func[2], func[3], ~func[4], ~func[5]);  // AND_Gate
  and and_2 (and_2_out, ~rt[1], ~rt[2]);  // AND_Gate
  and and_3 (and_3_out, ~rt[3], ~rt[4]);  // AND_Gate
  and and_4 (and_4_out, and_6_out, Op[0]);
  and and_5 (jr_jalr_detect, and_1_out, and_18_out);
  and and_6 (and_6_out, ~Op[3], ~Op[4], ~Op[5]);  // AND_Gate
  nand nand_1 (nand_1_out, Op[0], Op[1], Op[2]);
  and and_7 (and_7_out, Op[3], ~Op[4], ~Op[5]);  // AND_Gate
  and and_8 (and_8_out, ~Op[4], Op[5]);  // AND_Gate
  and and_9 (and_9_out, ~Op[2], Op[1], Op[0]);  // AND_Gate
  and and_10 (and_10_out, and_2_out, and_4_out, and_3_out);
  and and_11 (and_11_out, nand_1_out, and_7_out);
  and and_12 (and_12_out, and_6_out, Op[2]);
  and and_13 (and_13_out, Op[0], Op[1], Op[2], Op[3]);
  and and_14 (and_14_out, ~Op[0], ~Op[1], ~Op[2]);  // AND_Gate
  and and_15 (and_15_out, Op[1], ~Op[2]);  // AND_Gate
  and and_16 (and_16_out, and_8_out, and_9_out);
  or or_1 (ALUOp0, and_12_out, and_10_out);
  and and_17 (and_17_out, and_6_out, and_15_out);
  and and_18 (and_18_out, and_6_out, and_14_out);
  or or_2 (ALUOp1, and_18_out, and_13_out, and_11_out);
  or or_3 (ALUSrc, and_7_out, and_16_out, and_8_out);
  and and_19 (MemRead, and_8_out, ~Op[3]);  // AND_Gate
  and and_20 (MemWrite, and_8_out, Op[3]);
  or or_4 (or_4_out, ALUOp1, MemRead);
  and and_21 (RegWr, ~and_8_out, ~and_17_out, or_4_out, ~ALUOp0, ~jr_jalr_detect);  // AND_Gate
  not not_1 (RegDst, and_18_out);

  assign MemToReg = MemRead;
endmodule

// R Decoder
module ALUOpCoderRTypeInstruction (
  input  ALUOp1,
  input  ALUOp2,
  input  func5,
  input  func4,
  input  func3,
  input  func2,
  input  func1,
  input  func0,
  output op3,
  output op2,
  output op1,
  output op0,
  output movn,
  output movz,
  output shift_src,
  output JALR,
  output JR,
  output sltyes,
  output sltunsignedcheck
);

  wire and_3_out, and_4_out, and_5_out, and_6_out, and_7_out, and_8_out, and_9_out, and_10_out, and_11_out,
       and_12_out, and_13_out, and_14_out, and_15_out, not_1_out, not_2_out, not_3_out, not_4_out, not_5_out,
       not_6_out, not_7_out, not_8_out, not_9_out, not_10_out, not_11_out, not_12_out, not_13_out,
       not_14_out, not_15_out, not_16_out, not_17_out, not_18_out;

  and and_1 (op3, func5, func2);
  not not_1 (not_1_out, func3);
  and and_2 (op2, not_1_out, func1);
  not not_2 (not_2_out, ALUOp1);
  and and_3 (and_3_out, not_2_out, func3);
  and and_4 (and_4_out, func3, func1);
  and and_5 (and_5_out, func3, func2);
  and and_6 (and_6_out, func4, func3);
  and and_7 (and_7_out, func5, func0);
  and and_8 (and_8_out, func5, func3);
  and and_9 (and_9_out, ALUOp2, func3);
  not not_3 (not_3_out, ALUOp1);
  and and_10 (and_10_out, not_3_out, not_4_out, func0);
  not not_4 (not_4_out, func5);
  not not_5 (not_5_out, func5);
  and and_11 (and_11_out, not_5_out, not_6_out, func0);
  not not_6 (not_6_out, func3);
  not not_7 (not_7_out, func5);
  and and_12 (and_12_out, not_7_out, func1, func0);
  not not_8 (not_8_out, func5);
  and and_13 (and_13_out, not_8_out, func2);
  not not_9 (not_9_out, func5);
  and and_14 (and_14_out, not_9_out, func4, func0);
  and and_15 (and_15_out, ALUOp2, not_10_out, func0);
  not not_10 (not_10_out, func5);
  not not_11 (not_11_out, func5);
  not not_12 (not_12_out, func4);
  not not_13 (not_13_out, func2);
  not not_14 (not_14_out, func5);
  not not_15 (not_15_out, func4);
  not not_16 (not_16_out, func2);
  not not_17 (not_17_out, func0);
  and and_16 (JALR, func0, ~func1, ~func5, ~func4);  // AND_Gate
  and and_17 (JR, ~func4, ~func5, ~func1, func3, not_18_out);  // AND_Gate
  not not_18 (not_18_out, func0);
  and and_18 (sltyes, func5, ~func4, func3);  // AND_Gate
  and and_19 (movn, not_11_out, not_12_out, func3, not_13_out, func1, func0);
  and and_20 (movz, not_14_out, not_15_out, func3, not_16_out, func1, not_17_out);
  or or_1 (op1, and_3_out, and_4_out, and_5_out, and_6_out, and_7_out, and_8_out, and_9_out);
  or or_2 (op0, and_10_out, and_11_out, and_12_out, and_13_out, and_14_out, and_15_out);
  and and_21 (sltunsignedcheck, sltyes, func0);

  assign shift_src = func2;
endmodule

// I Decoder
module ALUImmediateOPCircuit (
  input  bit5,
  input  bit4,
  input  bit3,
  input  bit2,
  input  bit1,
  input  bit0,
  input  [4:0] rt,
  input  aluOp0,
  input  aluOp1,
  output op3,
  output op2,
  output op1,
  output op0,
  output bltz,
  output bgez,
  output sltunsigned,
  output sltyes,
  output j,
  output jal,
  output beq,
  output bne,
  output blez,
  output bgtz,
  output LUI
);

  wire and_1_out, and_2_out, and_3_out, and_4_out, and_5_out, and_6_out, and_7_out, and_14_out, and_16_out,
       and_17_out, and_18_out, and_22_out, and_23_out, and_26_out, not_1_out, not_2_out, not_3_out,
       not_4_out, not_5_out, not_6_out, not_7_out, not_8_out, not_9_out, not_10_out, not_11_out, not_12_out,
       not_13_out, not_14_out, not_15_out, not_16_out, not_17_out, not_18_out, not_19_out, not_20_out,
       not_21_out, not_22_out, not_23_out, not_24_out, not_25_out, not_26_out, not_27_out, not_28_out,
       not_29_out;

  and and_1 (and_1_out, bit3, bit2, not_1_out);
  not not_1 (not_1_out, bit1);
  and and_2 (and_2_out, bit3, bit2, not_2_out);
  not not_2 (not_2_out, bit0);
  not not_3 (not_3_out, bit5);
  not not_4 (not_4_out, bit3);
  and and_3 (and_3_out, not_3_out, not_4_out, bit2);
  and and_4 (and_4_out, bit2, bit1, not_5_out);
  not not_5 (not_5_out, bit0);
  not not_6 (not_6_out, bit2);
  and and_5 (and_5_out, not_6_out, not_7_out);
  not not_7 (not_7_out, bit1);
  not not_8 (not_8_out, bit3);
  and and_6 (and_6_out, not_8_out, bit2);
  and and_7 (and_7_out, bit2, bit0);
  not not_9 (not_9_out, bit3);
  and and_8 (op0, not_9_out, bit2);
  not not_10 (not_10_out, bit5);
  not not_11 (not_11_out, bit2);
  not not_12 (not_12_out, bit5);
  not not_13 (not_13_out, bit2);
  not not_14 (not_14_out, bit3);
  not not_15 (not_15_out, bit2);
  not not_16 (not_16_out, bit0);
  not not_17 (not_17_out, bit5);
  not not_18 (not_18_out, bit3);
  not not_19 (not_19_out, bit2);
  not not_20 (not_20_out, bit5);
  not not_21 (not_21_out, bit3);
  not not_22 (not_22_out, bit1);
  not not_23 (not_23_out, bit0);
  not not_24 (not_24_out, bit5);
  not not_25 (not_25_out, bit3);
  not not_26 (not_26_out, bit1);
  not not_27 (not_27_out, bit3);
  not not_28 (not_28_out, bit0);
  not not_29 (not_29_out, bit3);
  and and_9 (LUI, bit0, bit1, bit2, bit3, ~bit4, ~bit5);  // AND_Gate
  or or_1 (op3, and_1_out, and_2_out);
  or or_2 (op2, and_3_out, and_4_out);
  or or_3 (op1, and_5_out, and_6_out, and_7_out, bit5);
  and and_10 (sltunsigned, not_10_out, bit3, not_11_out, bit1, bit0);
  and and_11 (sltyes, not_12_out, bit3, not_13_out, bit1);
  and and_12 (j, not_14_out, not_15_out, not_16_out, bit1);
  and and_13 (jal, not_17_out, not_18_out, bit1, not_19_out, bit0);
  and and_14 (and_14_out, not_20_out, not_21_out, not_22_out, not_23_out);
  and and_15 (beq, and_14_out, and_23_out);
  and and_16 (and_16_out, not_24_out, not_25_out, not_26_out, bit0);
  and and_17 (and_17_out, not_27_out, bit2, bit1, not_28_out);
  and and_18 (and_18_out, not_29_out, bit2, bit1, bit0);
  and and_19 (bne, and_23_out, and_16_out);
  and and_20 (blez, and_23_out, and_17_out);
  and and_21 (bgtz, and_23_out, and_18_out);
  and and_22 (and_22_out, ~bit3, ~bit1, ~bit2, bit0);  // AND_Gate
  and and_23 (and_23_out, ~aluOp1, aluOp0);  // AND_Gate
  and and_24 (bgez, and_22_out, rt[0]);
  and and_25 (bltz, and_22_out, and_26_out);
  and and_26 (and_26_out, ~rt[0], ~rt[1], ~rt[2], ~rt[3], ~rt[4]);  // AND_Gate
endmodule

// ==
module IsEqual5 (
  input  [4:0] in_1,
  input  [4:0] in_2,
  output rA
);

  wire [4:0] xnor_1_out;

  assign xnor_1_out = ~(in_1 ^ in_2);  // XNOR_Gate xnor_1, 5 bits wide
  and and_1 (rA, xnor_1_out[0], xnor_1_out[1], xnor_1_out[2], xnor_1_out[3], xnor_1_out[4]);
endmodule

// ==0
module IsZero32 (
  input  [31:0] In,
  output Out
);

  nor nor_1 (Out, In[0], In[1], In[2], In[3], In[4], In[5], In[6], In[7], In[8], In[9], In[10], In[11], In[12], In[13], In[14], In[15], In[16], In[17], In[18], In[19], In[20], In[21], In[22], In[23], In[24], In[25], In[26], In[27], In[28], In[29], In[30], In[31]);
endmodule
